# Fritzing sketch diagram (saved by Fritzing 0.9.4)
breadboards: 1

parts:
  Raspberry_Pi_4 = Raspberry Pi 3 [part_number=RPI-3-V1.2]
  Part1 = Adafruit ADT7410 [part_number="Adafruit #4089"]

nets:
  3V3: Raspberry_Pi_4.3v3, Part1.VDD
  N1: Raspberry_Pi_4.GPIO2, Part1.SDA
  N2: Raspberry_Pi_4.GPIO3, Part1.SCL
  GND: Raspberry_Pi_4.GND, Part1.GND
